// Logisim project 4bitUniversalShiftRegister.circ as structural Verilog: 1 circuit, main circuit main
module main (
  input  I0,
  input  I1,
  input  I2,
  input  I3,
  input  in_5,
  input  in_6,
  input  [1:0] S,
  input  in_8,
  output [3:0] out_9
);

  wire clock_1_out, multiplexer_1_out, multiplexer_2_out, multiplexer_3_out, multiplexer_4_out;

  Clock clock_1 (.out(clock_1_out));
  Multiplexer #(.select(2)) multiplexer_1 (
    .in0(in_6), .in1(out_9[1]), .in2(I0), .in3(out_9[0]), .out(multiplexer_1_out), .sel(S));
  D_Flip_Flop d_ff_1 (.D(multiplexer_1_out), .clk(clock_1_out), .Q(out_9[0]), .reset(in_8));  // open: Qn, preset
  Multiplexer #(.select(2)) multiplexer_2 (
    .in0(out_9[0]), .in1(out_9[2]), .in2(I1), .in3(out_9[1]), .out(multiplexer_2_out), .sel(S));
  D_Flip_Flop d_ff_2 (.D(multiplexer_2_out), .clk(clock_1_out), .Q(out_9[1]), .reset(in_8));  // open: Qn, preset
  Multiplexer #(.select(2)) multiplexer_3 (
    .in0(out_9[1]), .in1(out_9[3]), .in2(I2), .in3(out_9[2]), .out(multiplexer_3_out), .sel(S));
  D_Flip_Flop d_ff_3 (.D(multiplexer_3_out), .clk(clock_1_out), .Q(out_9[2]), .reset(in_8));  // open: Qn, preset
  Multiplexer #(.select(2)) multiplexer_4 (
    .in0(out_9[2]), .in1(in_5), .in2(I3), .in3(out_9[3]), .out(multiplexer_4_out), .sel(S));
  D_Flip_Flop d_ff_4 (.D(multiplexer_4_out), .clk(clock_1_out), .Q(out_9[3]), .reset(in_8));  // open: Qn, preset
endmodule
